# Fritzing sketch OtoSeraArduinoDevresi (saved by Fritzing 0.9.3b)
breadboards: 1

parts:
  VCC1 = Battery block 9V
  Parça1 = Arduino Uno (Rev3)
  IC1 = L293D [package=THT]
  Parça2 = Bluetooth HC-05 Macho
  J1 = Basic Servo
  M1 = DC Motor

nets:
  GND: VCC1.-, Parça1.GND, IC1.0V, Parça2.GND, J1.gnd
  N1: VCC1.+, IC1.+Vmotor
  N2: Parça1.D9_PWM, J1.pulse
  N3: Parça1.D0/RX, Parça2.RXD
  N4: Parça1.D1/TX, Parça2.TXD
  N5: Parça1.D5_PWM, IC1.Enable_1
  N6: Parça1.D6_PWM, IC1.In_1
  N7: Parça1.D7, IC1.In_2
  VCC: Parça1.5V, IC1.+V, Parça2.VCC, J1.vcc
  N8: IC1.Out_1_(_Controlled_by_Enable_1_), M1.pin_2
  N9: IC1.Out_2_(_Controlled_by_Enable_1_), M1.pin_1
